# Fritzing sketch Z3-Gate-Halfadder (saved by Fritzing 1.0.1rc)
breadboards: 1

parts:
  GV5-1 = Omron_MY2K_02_12VDC_3A [part_number=GV5-2 package=THT]
  GV5-2 = Omron_MY2K_02_12VDC_3A [part_number=GV5-2 package=THT]
  D1 = Diode [package=diode-1n4148]
  D2 = Diode [package=diode-1n4148]
  R1 = Resistor [tolerance=±5% resistance=220 package="2512 [SMD]"]  # not connected
  LED1 = smd LED [color="Orange (620nm)" package="0603 [SMD]"]  # not connected
  LED2 = smd LED [color="Yellow (592nm)" package="0603 [SMD]"]  # not connected
  S1 = Momentary Switch [package=ksa_sealed_tac_switch]
  S2 = Momentary Switch [package=ksa_sealed_tac_switch]

nets:
  N1: GV5-1.Out_2-2, GV5-2.Out_2-2, S1.1, S2.1, S2.3
  N2: GV5-1.Set/Reset#89, GV5-2.Out_2-1, GV5-2.Set/Reset#89
  N3: GV5-1.Set/Reset#90, D2.C, S1.2
  N4: GV5-2.Set/Reset#90, D1.C, S2.2

custom parts:
  Omron_MY2K_02_12VDC_3A: Omron GV5-2, 12VDC @ 2 Amp, Bistable, Low Signal Relay, DPDT, No Coil Polarity
